# Fritzing sketch UARt (saved by Fritzing 0.9.3b)

parts:
  Part1 = Arduino Mega ADK (Rev3)
  Part2 = Arduino Mega ADK (Rev3)

nets:
  N1: Part1.D15/RX3, Part2.D14/TX3
  N2: Part1.D14/TX3, Part2.D15/RX3
  GND: Part1.GND, Part2.GND
