# Fritzing sketch Untitled Sketch 2 (saved by Fritzing 0.9.3b)
breadboards: 1

parts:
  Part1 = Arduino Uno (Rev3)
  LED1 = LED - 5mm [color="Red (633nm)" package="5 mm [THT]"]

nets:
  N1: Part1.D8, LED1.anode
  N2: Part1.D9_PWM, LED1.cathode

// code stored in the sketch: Untitled2.ino
void setup()
{
pinMode(8,OUTPUT);
pinMode(9,OUTPUT);
Serial.begin(9600);
}
void loop()
{
digitalWrite(8,HIGH);
digitalWrite(9,LOW);
Serial.println("ON");
delay(1000);
digitalWrite(8,LOW);
digitalWrite(9,LOW);
Serial.println("OFF");
delay(1000);
}
