# Fritzing sketch bluetooth (saved by Fritzing 0.9.3b)

parts:
  Part2 = Arduino Mega ADK (Rev3)
  Part3 = Bluetooth HC-05 Macho

nets:
  GND: Part2.GND, Part3.GND

// code stored in the sketch: Untitled2.ino
void setup()
{
pinMode(8,OUTPUT);
pinMode(9,OUTPUT);
Serial.begin(9600);
}
void loop()
{
digitalWrite(8,HIGH);
digitalWrite(9,LOW);
Serial.println("ON");
delay(1000);
digitalWrite(8,LOW);
digitalWrite(9,LOW);
Serial.println("OFF");
delay(1000);
}
