# Fritzing sketch ir (saved by Fritzing 0.9.3b)

parts:
  D1 = LTE-302 [package=lte-302]
  Part1 = Arduino Uno (Rev3)
  R1 = Resistor [tolerance=±5% resistance=220 package=THT]
  Part2 = Arduino Leonardo (Rev3b)
  IR1 = TSOP312.., 314.. [package=THT]

nets:
  N1: D1.A, R1.Pin_0
  N2: D1.C, Part1.GND
  N3: Part1.D3_PWM, R1.Pin_1
  N4: Part2.D0/RX, IR1.Data
  N5: Part2.3V3, IR1.Vs
  GND: Part2.GND, IR1.GND
