# Fritzing sketch lifi (saved by Fritzing 0.9.3b)
perfboards: 1

parts:
  Rx = Photocell (LDR) [package=THT]  # not connected
  R3 = Resistor [tolerance=±5% resistance=270 package=THT]
  R4 = Resistor [tolerance=±5% resistance=270 package=THT]
  Tx = LED - 3mm [color="Red (633nm)" package="3 mm [THT]"]
  Part1 = Arduino Mega ADK (Rev3)

nets:
  N1: R3.Pin_0, R4.Pin_1, Part1.GND
  N2: R3.Pin_1, Tx.cathode
  N3: R4.Pin_0, Part1.A0
  N4: Tx.anode, Part1.D22
