# Fritzing sketch nrf (saved by Fritzing 0.9.3b)

parts:
  Part1 = Arduino Mega ADK (Rev3)
  Part2 = NRF24L01+ Breakout Board

nets:
  N1: Part1.D8_PWM, Part2.CS
  3V3: Part1.3V3, Part2.VCC
  N2: Part1.D7_PWM, Part2.CE
  N3: Part1.D50/MISO, Part2.MISO
  N4: Part1.D51/MOSI, Part2.MOSI
  N5: Part1.D52/SCK, Part2.SCK
  GND: Part1.GND, Part2.GND
