# Fritzing sketch rfid (saved by Fritzing 0.9.3b)

parts:
  Part1 = Arduino Mega ADK (Rev3)
  U1 = RFID RC522 SIP - 8 pins [chip_label="RFID RC522" package="SIP (Single Inline) [THT]"]

nets:
  GND: Part1.GND, U1.GND
  3V3: Part1.3V3, U1.VCC
  N1: Part1.D5_PWM, U1.RST
  N2: Part1.D50/MISO, U1.MISO
  N3: Part1.D51/MOSI, U1.MOSI
  N4: Part1.D52/SCK, U1.SCK
  N5: Part1.D53/SS, U1.NSS

custom parts:
  RFID RC522 SIP - 8 pins: A SIP stand-in part for RFID RC522 . With 8 pins on a 300 mil single inline package (SIP) footprint.
